# Fritzing sketch arduino_lie_detector (saved by Fritzing 0.8.7b)
breadboards: 1

parts:
  Onderdeel1 = Arduino Nano (Rev3.0)
  LED1 = LED - 5mm [color="Green (555nm)" package="5 mm [THT]"]
  LED2 = LED - 5mm [color="Orange (620nm)" package="5 mm [THT]"]
  LED3 = LED - 5mm [color="Red (633nm)" package="5 mm [THT]"]
  R2 = Resistor [tolerance=±5% resistance=1k package=THT]
  R3 = Resistor [tolerance=±5% resistance=220 package=THT]
  R4 = Resistor [tolerance=±5% resistance=220 package=THT]
  R5 = Resistor [tolerance=±5% resistance=220 package=THT]

nets:
  N1: Onderdeel1.GND, LED1.cathode, LED2.cathode, LED3.cathode
  N2: Onderdeel1.A0, R2.Pin_1
  N3: LED1.anode, R5.Pin_1
  N4: LED2.anode, R4.Pin_1
  N5: LED3.anode, R3.Pin_1

notes:
  Wires go to the finger clip.
